// Logisim project SISTEMA PARA IDENTIFICAR A SEQUÊNCIA 0001101.circ as structural Verilog: 1 circuit, main circuit main
module main (
  input  ENTRADA,
  output SAIDA
);

  wire _1_q, _2_q, _3_q, and_1_out, and_2_out, and_3_out, and_4_out, and_5_out, and_6_out, and_7_out,
       CLOCK_out, or_1_out, or_2_out, or_3_out, or_4_out, or_5_out, or_6_out, RESETAR_out;

  or or_1 (or_1_out, _1_q, ~ENTRADA);  // OR_Gate
  Clock CLOCK (.out(CLOCK_out));
  Button RESETAR (.out(RESETAR_out));
  or or_2 (or_2_out, ~_3_q, _2_q, ~_1_q, ENTRADA);  // OR_Gate
  and and_1 (and_1_out, _2_q, _1_q, ENTRADA);
  and and_2 (and_2_out, or_2_out, or_1_out);
  J_K_Flip_Flop _3 (
    .J(and_1_out), .clk(CLOCK_out), .K(and_2_out), .Q(_3_q), .reset(RESETAR_out));  // open: Qn, preset, en
  and and_3 (and_3_out, _3_q, _1_q);
  and and_4 (and_4_out, ~_3_q, ENTRADA);  // AND_Gate
  or or_3 (or_3_out, and_3_out, and_4_out);
  and and_5 (and_5_out, _1_q, ~ENTRADA);  // AND_Gate
  J_K_Flip_Flop _2 (
    .J(and_5_out), .clk(CLOCK_out), .K(or_3_out), .Q(_2_q), .reset(RESETAR_out));  // open: Qn, preset, en
  or or_4 (or_4_out, ~_3_q, ~_2_q, ENTRADA);  // OR_Gate
  or or_5 (or_5_out, _3_q, ~ENTRADA);  // OR_Gate
  and and_6 (and_6_out, or_4_out, or_5_out);
  or or_6 (or_6_out, ~_2_q, ENTRADA);  // OR_Gate
  J_K_Flip_Flop _1 (
    .J(and_6_out), .clk(CLOCK_out), .K(or_6_out), .Q(_1_q), .reset(RESETAR_out));  // open: Qn, preset, en
  and and_7 (and_7_out, _3_q, _2_q, ~_1_q, ENTRADA);  // AND_Gate
  D_Flip_Flop d_ff_1 (.clk(CLOCK_out), .D(and_7_out), .Q(SAIDA), .reset(RESETAR_out));  // open: Qn, preset, en
endmodule
